# Fritzing sketch montage_moteurs (saved by Fritzing 0.9.2b)

parts:
  Raspberry_Pi1 = Raspberry Pi 2
  U1 = L298 [package=multiwatt15]
  M1 = DC Motor
  M2 = DC Motor
  VCC1 = 4 x AAA Battery Mount
  VCC2 = Battery block 9V
  U3 = IC, SIP package, 4 pins [chip_label="Encoder quadrature" part_number="encoder quadrature"]
  U4 = IC, SIP package, 4 pins [chip_label="Encoder quadrature" part_number="encoder quadrature"]
  R1 = Resistor [tolerance=±5% resistance=2.2k package=THT]
  R2 = Resistor [tolerance=±5% resistance=2.2k package=THT]
  R3 = Resistor [tolerance=±5% resistance=3.3k package=THT]
  R4 = Resistor [tolerance=±5% resistance=3.3k package=THT]
  R5 = Resistor [tolerance=±5% resistance=2.2k package=THT]
  R6 = Resistor [tolerance=±5% resistance=3.3k package=THT]
  R7 = Resistor [tolerance=±5% resistance=2.2k package=THT]
  R8 = Resistor [tolerance=±5% resistance=3.3k package=THT]
  C1 = Ceramic Capacitor [capacitance=10nF package="100 mil [THT, multilayer]"]
  C2 = Ceramic Capacitor [capacitance=10nF package="100 mil [THT, multilayer]"]
  C3 = Electrolytic Capacitor [capacitance=0.1mF voltage=16V package="100 mil [THT, electrolytic]"]

nets:
  N1: Raspberry_Pi1.GPIO4, U4.pin4, R5.Pin_1, R6.Pin_0
  GND: Raspberry_Pi1.GND, U1.GND, VCC1.-, VCC2.-, U3.pin2, U4.pin2, R3.Pin_1, R4.Pin_1, R6.Pin_1, R8.Pin_1, C3.-
  N2: Raspberry_Pi1.GPIO17, U4.pin3, R7.Pin_1, R8.Pin_0
  N3: Raspberry_Pi1.GPIO13, U1.ENB
  N4: Raspberry_Pi1.GPIO21, U3.pin3, R2.Pin_1, R4.Pin_0
  N5: Raspberry_Pi1.GPIO20, U3.pin4
  N6: Raspberry_Pi1.GPIO12, U1.IN4
  N7: Raspberry_Pi1.GPIO25, U1.IN3
  N8: Raspberry_Pi1.GPIO24, U1.IN2
  N9: Raspberry_Pi1.GPIO23, U1.IN1
  N10: Raspberry_Pi1.GPIO18, U1.ENA
  N11: Raspberry_Pi1.5V, U1.VLS, VCC1.+
  N12: U1.OUT1, M2.pin_1, C1.1
  N13: U1.OUT2, M2.pin_2, C1.0
  N14: U1.VS, VCC2.+, C3.+
  N15: U1.OUT3, M1.pin_1, C2.1
  N16: U1.OUT4, M1.pin_2, C2.0
  5V: U3.pin1, U4.pin1, R1.Pin_0, R2.Pin_0, R5.Pin_0, R7.Pin_0
  N17: R1.Pin_1, R3.Pin_0
